# Fritzing sketch Ard1-Arduino (saved by Fritzing 0.9.2b)
circuit board: 8.46667cm x 5.64444cm
breadboards: 1

parts:
  LED1 = LED - 3mm [color="Green (570nm)" package="3 mm [THT]"]
  Part1 = Arduino Uno (Rev3)
  R1 = Resistor [tolerance=±5% resistance=270 package=THT]
  R2 = Resistor [tolerance=±5% resistance=270 package=THT]
  LED2 = LED - 3mm [color="Red (635nm)" package="3 mm [THT]"]
  R3 = Resistor [tolerance=±5% resistance=10k package=THT]
  R6 = PHOTOCELL [package=photocell]
  R7 = Resistor [tolerance=±5% resistance=10k package=THT]
  S1 = Momentary Switch [package=ksa_sealed_tac_switch]

nets:
  N1: LED1.cathode, Part1.GND, R1.Pin_1, R6.P$1, R7.Pin_1
  N2: LED1.anode, R2.Pin_0
  N3: Part1.A5/SCL, R3.Pin_0, R6.P$2
  N4: Part1.D11_PWM/MOSI, LED2.anode
  N5: Part1.D2, R7.Pin_0, S1.1
  N6: Part1.5V, R2.Pin_1, R3.Pin_1, S1.3
  N7: R1.Pin_0, LED2.cathode
