# Fritzing sketch Ard1-Sensors (saved by Fritzing 0.9.2b)
breadboards: 1

parts:
  R1 = Resistor [tolerance=±5% resistance=270 package=THT]
  R2 = Resistor [tolerance=±5% resistance=270 package=THT]
  LED2 = LED - 3mm [color="Red (635nm)" package="3 mm [THT]"]
  R3 = Resistor [tolerance=±5% resistance=20k package=THT]
  R6 = PHOTOCELL [package=photocell]
  R7 = Resistor [tolerance=±5% resistance=10k package=THT]
  S1 = Momentary Switch [package=ksa_sealed_tac_switch]
  LED7 = LED - 3mm [color="Green (570nm)" current=10mA package="3 mm [THT]"]
  C1 = Capacitor [package=cap-pth-small2]
  U1 = TMP36 [package=to-92]
  R8 = Resistor [tolerance=±5% resistance=22k package=THT]
  R9 = Resistor [tolerance=±5% resistance=10k package=THT]

nets:
  N1: R1.Pin_0, LED2.cathode
  N2: R1.Pin_1, R6.P$2, R7.Pin_1, LED7.cathode, R9.Pin_0
  N3: R2.Pin_0, LED7.anode
  N4: R2.Pin_1, S1.3, R8.Pin_0
  N5: R3.Pin_0, R6.P$1
  N6: R7.Pin_0, S1.2
  N7: C1.1, U1.VCC, R8.Pin_1
  N8: C1.2, U1.GND, R9.Pin_1

notes:
  BTN
  LED
  LIGHT
  TEMP
