# Fritzing sketch Ard2 - Actuators (saved by Fritzing 0.9.2b)
breadboards: 1

parts:
  J1 = Piezo Speaker  # not connected
  J2 = Power Jack [package=power_jack_pth]  # not connected
  IC1 = ULN2803A [package=THT]  # not connected
  M1 = DC Motor [part_number=12VDC]  # not connected
  NEOPIXEL1 = Neopixel Strip -- Black (60/m)  # not connected
  U2 = XBEE-1 [package=xbee-1]
  J3 = Power Jack [package=power_jack_pth]

nets:
  N1: U2.VDD, J3.PWR
  GND: U2.GND, J3.GND

notes:
  BUZZER
  +3.3V
  +12V

custom parts:
  Neopixel Strip -- Black (60/m): Neopixel Strip, Black, 60 pixels per meter.
