# Fritzing sketch DemoGroveBoard (saved by Fritzing 0.9.3b)
circuit board: 7cm x 5cm
breadboards: 1

parts:
  LED1 = LED - 5mm [color="Red (633nm)" package="5 mm [THT]"]
  R1 = Resistor [tolerance=±5% resistance=220 package=THT]
  OMRON1 = OMRON PCB Power Relay – G5LE [part_number="G5LE-1\n" package=THT]
  J2 = female pin header, 4 pins [form="♀ (female)"]
  R2 = Resistor [tolerance=±5% resistance=220 power=125mW package=THT]
  LED2 = LED - 3mm [color="Green (570nm)" package="3 mm [THT]"]
  JACK1 = 2.1mm Barrel Jack with Terminal Block

nets:
  N1: LED1.cathode, J2.pin1, LED2.cathode, JACK1.NEG
  N2: LED1.anode, R1.Pin_0
  N3: R1.Pin_1, J2.pin2
  N4: OMRON1.COIL1, OMRON1.COIL2
  N5: J2.pin4, R2.Pin_0
  N6: R2.Pin_1, LED2.anode
