# Fritzing sketch ESP8266-ILI9341 LCD (saved by Fritzing 0.9.3b)
breadboards: 1

parts:
  U1 = NodeMCU V3.0
  TFT1 = Color 320x240 TFT Display, ILI9341 Controller Chip

nets:
  N1: U1.D1, TFT1.Reset
  N2: U1.D4, TFT1.D/C
  3V3: U1.3V3, TFT1.VCC
  N3: U1.GND#6, U1.GND#13, U1.GND#16, U1.GND#33, TFT1.GND, TFT1.LED
  N4: U1.D5, TFT1.SCK
  N5: U1.D6, TFT1.SDO_(MISO)
  N6: U1.D7, TFT1.SDI_(MOSI)
  N7: U1.D8, TFT1.CS

notes:
  BE CAREFUL!!!!
  The connections are correct!
  VCC GND CS RESET D/C MOSI CLOCK  LED MISO
  The pinout is incomplete
  320x240 2.8" TFT ILI9341

custom parts:
  NodeMCU V3.0: ESP8266 based NodeMCU
  Color 320x240 TFT Display, ILI9341 Controller Chip: 2.2" TFT Display with ILI9341 Controller
