# Fritzing sketch ESP_expansion_board (saved by Fritzing 0.9.3b)
breadboards: 2

parts:
  U1 = NodeMCU V1.0
  S1 = Pushbutton [package="[THT]"]
  U2 = Header 1 [package=1x01_offset]
  U3 = Header 1 [package=1x01_offset]
  U4 = Header 1 [package=1x01_offset]
  J1 = Power Jack [package=power_jack_pth]
  D1 = Schottky Diode [part_number=1N5817 package="300 mil [THT]"]
  R1 = Resistor Mini [tolerance=±5% resistance=220 package=THT]
  LED1 = LED - 3mm [color="Blue (430nm)" package="3 mm [THT]"]
  U5 = Voltage Regulator - 3.3V [package="TO220 [THT]"]
  LED2 = LED - 3mm [color="Red (633nm)" package="3 mm [THT]"]
  LED3 = LED - 3mm [color="Yellow (592nm)" package="3 mm [THT]"]
  LED4 = LED - 3mm [color="Green (560nm)" package="3 mm [THT]"]
  R2 = Resistor Mini [tolerance=±5% resistance=3.3k package=THT]
  R3 = Resistor Mini [tolerance=±5% resistance=3.3k package=THT]
  U6 = Header 1 [package=1x01_offset]
  U7 = Header 1 [package=1x01_offset]
  U8 = Header 1 [package=1x01_offset]
  U9 = Header 1 [package=1x01_offset]
  U10 = Header 1 [package=1x01_offset]  # not connected
  U11 = Header 1 [package=1x01_offset]  # not connected
  U12 = Header 1 [package=1x01_offset]
  U13 = Header 1 [package=1x01_offset]
  U14 = Header 1 [package=1x01_offset]
  U15 = Header 1 [package=1x01_offset]
  U16 = Header 1 [package=1x01_offset]  # not connected
  U17 = Header 1 [package=1x01_offset]  # not connected
  U18 = Header 1 [package=1x01_offset]
  U19 = Header 1 [package=1x01_offset]
  U20 = Header 1 [package=1x01_offset]  # not connected
  U21 = Header 1 [package=1x01_offset]
  U22 = Header 1 [package=1x01_offset]
  U23 = Header 1 [package=1x01_offset]  # not connected
  U24 = Header 1 [package=1x01_offset]
  U25 = Header 1 [package=1x01_offset]
  S3 = Pushbutton [package="[THT]"]
  U26 = Header 1 [package=1x01_offset]
  U27 = Header 1 [package=1x01_offset]
  U28 = Header 1 [package=1x01_offset]
  U29 = Header 1 [package=1x01_offset]
  R4 = Resistor Mini [tolerance=±5% resistance=3.3k package=THT]
  R5 = Resistor Mini [tolerance=±5% resistance=3.3k package=THT]
  R6 = Resistor Mini [tolerance=±5% resistance=3.3k package=THT]
  U30 = Header 1 [package=1x01_offset]
  U31 = TLP621 [package=THT]  # not connected
  J2 = Camdenboss CTB0158-4 [part_number=CTB0158-4 package=THT]  # not connected
  U32 = TLP621 [package=THT]  # not connected
  U33 = Header 1 [package=1x01_offset]
  U34 = Header 1 [package=1x01_offset]
  U35 = Header 1 [package=1x01_offset]
  R7 = Resistor Mini [tolerance=±5% resistance=220 package=THT]
  R8 = Resistor Mini [tolerance=±5% resistance=220 package=THT]

nets:
  N1: U1.D0, S1.Pin_1, S1.Pin_2, U3.1, U4.1
  N2: U1.D1, R3.Pin_0, U6.1, U14.1, U21.1
  N3: U1.D2, R2.Pin_0, U9.1, U15.1, U22.1
  N4: U1.D3, R4.Pin_0
  N5: U1.D4, R5.Pin_0
  N6: U1.3V3, D1.cathode, R1.Pin_1, R2.Pin_1, R3.Pin_1, U8.1, U13.1, U19.1, U27.1, U33.1
  GND: U1.GND, S1.Pin_3, S1.Pin_4, J1.GND, J1.GNDBREAK, LED1.cathode, U5.GND, LED2.cathode, LED3.cathode, LED4.cathode, U7.1, U12.1, U18.1, S3.Pin_3, S3.Pin_4, U26.1, U29.1, U34.1
  N7: U1.D5, R8.Pin_0
  N8: U1.D6, R7.Pin_0
  N9: U1.D7, U35.1
  N10: U1.D8, R6.Pin_0
  N11: U1.RX, U25.1
  N12: U1.TX, U24.1
  N13: U1.RST, U2.1
  N14: U1.SD3, S3.Pin_1, S3.Pin_2
  N15: U1.A0, U30.1
  N16: J1.PWR, U5.input_voltage, U28.1
  N17: D1.anode, U5.output_voltage
  N18: R1.Pin_0, LED1.anode
  N19: LED2.anode, R6.Pin_1
  N20: LED3.anode, R5.Pin_1
  N21: LED4.anode, R4.Pin_1

notes:
  SCL
  SDA
  I2C SECTION
  UART
  POWER ON
  RESET
  ANALOG
  OUT   IN   OUT   IN
  OPTO
  USER  B1   B2
  GND IO13 3V3
  SCHOTTKY

custom parts:
  NodeMCU V1.0: ESP8266 based NodeMCU
  Resistor Mini: A generic resistor (0.25W)
